# Fritzing sketch 回路図 (saved by Fritzing 0.9.3b)
circuit board: 9.51764cm x 5.64444cm
breadboards: 2

parts:
  LED1 = LEDs [package=led10mm]
  LED2 = LEDs [package=led10mm]
  R1 = Resistor [tolerance=±5% resistance=390 package=THT]
  S2 = Pushbutton [package="[SMD]"]
  S4 = Pushbutton [package="[SMD]"]
  S5 = Pushbutton [package="[SMD]"]
  Layer_SW = Pushbutton [package="[SMD]"]
  R2 = Resistor [tolerance=±5% resistance=390 package=THT]
  Teensy_3_2 = Teensy 3.1
  S1 = Pushbutton [package="[SMD]"]
  S3 = Pushbutton [package="[SMD]"]

nets:
  N1: LED1.C, LED1.A, LED2.C, LED2.A, R1.Pin_1, R2.Pin_1, Teensy_3_2.GND
  N2: R1.Pin_0, Teensy_3_2.A0/D14
  N3: S2.Pin_1, S2.Pin_2, S4.Pin_1, S4.Pin_2, S5.Pin_1, S5.Pin_2, Layer_SW.Pin_1, Layer_SW.Pin_2, Teensy_3_2.D5, S1.Pin_1, S1.Pin_2, S3.Pin_1, S3.Pin_2
  N4: S2.Pin_3, S2.Pin_4, Teensy_3_2.D7
  N5: S4.Pin_3, S4.Pin_4, Teensy_3_2.D9
  N6: S5.Pin_3, S5.Pin_4, Teensy_3_2.D10
  N7: Layer_SW.Pin_3, Layer_SW.Pin_4, Teensy_3_2.D11
  N8: R2.Pin_0, Teensy_3_2.A1/D15
  N9: Teensy_3_2.D6, S1.Pin_3, S1.Pin_4
  N10: Teensy_3_2.D8, S3.Pin_3, S3.Pin_4
